# Fritzing sketch diagrama (saved by Fritzing 0.9.3b)
breadboards: 1

parts:
  Componente1 = Arduino Nano (Rev3.0)
  S1 = Pushbutton [package="[SMD]"]
  S2 = Pushbutton [package="[SMD]"]
  S3 = Pushbutton [package="[SMD]"]
  ZS-042_RTC1 = ZS-042 RTC Module
  LCD2004-I2C1 = LCD2004-I2C
  2_Channel_Relay1 = 2 Channel Power Relay
  2_Channel_Relay2 = 2 Channel Power Relay
  HC-SR04_Sensor_1 = HC-SR04 Ultrasonic Distance Sensor
  DHT1 = DHT22 Humidity and Temperature Sensor
  J1 = Piezo Speaker

nets:
  GND: Componente1.GND, S1.Pin_3, S1.Pin_4, S2.Pin_3, S2.Pin_4, S3.Pin_3, S3.Pin_4, ZS-042_RTC1.GND, LCD2004-I2C1.GND, 2_Channel_Relay1.GND, 2_Channel_Relay2.GND, HC-SR04_Sensor_1.GND, DHT1.GND, J1.pin1
  N1: Componente1.D2, S1.Pin_1, S1.Pin_2
  N2: Componente1.D3, S2.Pin_1, S2.Pin_2
  N3: Componente1.D4, S3.Pin_1, S3.Pin_2
  N4: Componente1.D5, DHT1.DATA
  N5: Componente1.D6, J1.pin2
  N6: Componente1.D8, 2_Channel_Relay1.IN1
  N7: Componente1.D9, 2_Channel_Relay1.IN2
  N8: Componente1.D10, 2_Channel_Relay2.IN1
  N9: Componente1.D11/MOSI, 2_Channel_Relay2.IN2
  VCC: Componente1.5V, ZS-042_RTC1.VCC, LCD2004-I2C1.VCC, 2_Channel_Relay1.VCC, 2_Channel_Relay2.VCC, HC-SR04_Sensor_1.VCC, DHT1.VDD
  N10: Componente1.A3, HC-SR04_Sensor_1.TRIG
  N11: Componente1.A2, HC-SR04_Sensor_1.ECHO
  N12: ZS-042_RTC1.SDA, LCD2004-I2C1.SDA
  N13: ZS-042_RTC1.SCL, LCD2004-I2C1.SCL

custom parts:
  LCD2004-I2C: A standard character display with 4x20 characters. Comes in many colors with LCM2004 IIC attached.
  2 Channel Power Relay: A 2 channel power relay. The module operates at 5V.
